# Fritzing sketch automation (saved by Fritzing 0.8.7b)

parts:
  U1 = NodeMCU V1.0
  M1 = DC Motor
  KY-1 = Keyes Relay [package=THT]
  Q1 = TRANSISTOR_NPN [package=to-92-ammo]
  R1 = Resistor [tolerance=±5% resistance=220 package=THT]
  L1 = Inductor [package="0603 [SMD]"]
  VCC1 = Battery
  KY-2 = Keyes Relay [package=THT]
  Q2 = TRANSISTOR_NPN [package=to-92-ammo]
  R2 = Resistor [tolerance=±5% resistance=220 package=THT]

nets:
  N1: U1.D0, R1.Pin_1
  N2: U1.D1, R2.Pin_1
  N3: U1.GND, KY-1.ground, Q1.C, KY-2.ground
  N4: U1.Vin, KY-1.power
  N5: M1.pin_1, KY-1.NO
  N6: KY-1.signal, Q1.E
  N7: KY-1.C, VCC1.+
  N8: Q1.B, R1.Pin_0
  N9: L1.pin_0, KY-2.NO
  N10: KY-2.signal, Q2.E
  N11: Q2.B, R2.Pin_0

custom parts:
  NodeMCU V1.0: ESP8266 based NodeMCU
  Keyes Relay: The Keyes 5V relay module is suitable for SCM development, home appliance control. It uses a 5V~12V TIL control signal which can control DC / AC signal.
