# Fritzing sketch eye_blink (saved by Fritzing 0.8.7b)

parts:
  Part1 = Arduino Pro Mini v13
  Part2 = Max Power IR LED Kit
  J1 = Piezo Speaker

nets:
  GND: Part1.GND, Part2.GND, J1.pin1
  VCC: Part1.VCC, Part2.VCC
  N1: Part1.D4, J1.pin2
  N2: Part1.D3_PWM, Part2.CONTROL
