# Fritzing sketch fall_detect (saved by Fritzing 0.8.7b)
breadboards: 1

parts:
  Part1 = Triple Axis Gyro Breakout ITG-3200
  Part2 = Arduino Uno (Rev3) - ICSP
  LED1 = LED - 5mm [color="Red (633nm)" package="5 mm [THT]"]
  J1 = Piezo Speaker

nets:
  VCC: Part1.VCC, Part2.5V
  GND: Part1.GND, Part2.GND, LED1.cathode, J1.pin1
  N1: Part1.SDA, Part2.A4/SDA
  N2: Part1.SCL, Part2.A5/SCL
  N3: Part2.D11_PWM/MOSI, J1.pin2
  N4: Part2.D7, LED1.anode
