# Fritzing sketch novel industry (saved by Fritzing 0.8.7b)
breadboards: 1

parts:
  Part1 = Arduino Uno (Rev3) - ICSP
  LCD2 = LCD screen
  Part2 = Adafruit INA169 Analog DC Current Sensor Breakout [part_number="Adafruit #1164"]
  SW-1 = Vibration sensor module
  J1 = Piezo Speaker
  L1 = Inductor [package="0603 [SMD]"]
  VCC1 = Battery

nets:
  N1: Part1.A0, Part2.OUT
  N2: Part1.A1, SW-1.Digital_output
  N3: Part1.ICSP_MOSI, Part1.D11_PWM/MOSI, J1.pin2
  VCC: Part1.5V, Part2.VCC, SW-1.vcc
  GND: Part1.GND, LCD2.VSS, LCD2.V0, LCD2.R/W, LCD2.LED-, Part2.GND, SW-1.Ground, J1.pin1
  N4: Part1.D2, LCD2.DB7
  N5: Part1.D3_PWM, LCD2.DB6
  N6: Part1.D4, LCD2.DB5
  N7: Part1.D5_PWM, LCD2.DB4
  N8: Part1.D6_PWM, LCD2.E
  N9: Part1.D7, LCD2.RS
  3V3: Part1.3V3, LCD2.VDD
  N10: Part1.VIN, LCD2.LED+
  N11: Part2.VIN-, VCC1.+
  N12: Part2.VIN+, L1.pin_0

custom parts:
  Adafruit INA169 Analog DC Current Sensor Breakout: This breakout board will solve all your current-monitoring problems. Instead of struggling with a multimeter, you can just use the handy INA169 chip on this breakout to both measure both the DC current draw and have a handy analog output that is with respect to ground. The analog output makes this an ideal breakout for feedback-loop control. Most current-measuring devices such as our current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
  Vibration sensor module: Single-roller type full induction trigger switch. When no vibration or tilt, the product is ON conduction state, and in the steady state, when a vibration or tilt, the switch will be rendered instantly disconnect the conductive resistance increases, generating a current pulse signal, thereby triggering circuit. The default state of the swith is close Digital output Supply voltage:3.3V-5V On-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
