# Fritzing sketch petrol_pump (saved by Fritzing 0.8.7b)
breadboards: 1

parts:
  Part2 = Arduino Uno (Rev3) - ICSP
  J1 = Piezo Speaker
  U1 = RF-LINK_TX [package=rf-link_tx]
  U2 = RF-LINK_RX [package=rf-link_rx]
  Water_Level_Sensor1 = Water Level Sensor

nets:
  N1: Part2.A0, Water_Level_Sensor1.SIG
  N2: Part2.D11_PWM/MOSI, J1.pin2
  GND: Part2.GND, J1.pin1, U1.GND, U2.GND
  N3: Part2.D3_PWM, U2.DATA
  +5V: Part2.5V, U1.+5V, U2.+5V, Water_Level_Sensor1.VCC

custom parts:
  Water Level Sensor: A water level sensor. This sensor operates at 3V to 5V. The Sig (signal) pin outputs an analogue signal that is in proportion to the amount of water in contact with the sensor.
