# Fritzing sketch sms_notice (saved by Fritzing 0.8.7b)
breadboards: 1

parts:
  Part1 = Arduino Uno (Rev3) - ICSP
  LCD2 = LCD screen
  Part2 = Arduino Cellular Shield

nets:
  GND: Part1.GND, LCD2.VSS, LCD2.V0, LCD2.R/W, LCD2.LED-, Part2.GND
  N1: Part1.D0/RX, Part2.TX-O
  N2: Part1.D1/TX, Part2.RX-I
  N3: Part1.D2, LCD2.DB7
  N4: Part1.D3_PWM, LCD2.DB6
  N5: Part1.D4, LCD2.DB5
  N6: Part1.D5_PWM, LCD2.DB4
  N7: Part1.D6_PWM, LCD2.E
  N8: Part1.D7, LCD2.RS
  3V3: Part1.3V3, LCD2.VDD
  N9: Part1.VIN, LCD2.LED+
