# Fritzing sketch track (saved by Fritzing 0.8.7b)
breadboards: 1

parts:
  Part1 = Arduino Uno (Rev3) - ICSP
  U3 = HC-SR04 [chip_label=IC package="SIP (Single Inline) [THT]"]
  Part2 = Triple Axis Accelerometer Breakout - ADXL335
  LED1 = LED - 5mm [color="Red (633nm)" package="5 mm [THT]"]
  J1 = Piezo Speaker

nets:
  N1: Part1.A0, Part2.XOUT
  N2: Part1.A1, Part2.YOUT
  N3: Part1.A2, Part2.ZOUT
  N4: Part1.D12/MISO, U3.Echo
  N5: Part1.D13/SCK, U3.Trig
  5V: Part1.5V, Part2.VCC
  GND: Part1.GND, U3.GND, Part2.GND, LED1.cathode, J1.pin1
  VIN: Part1.VIN, U3.Vcc

custom parts:
  HC-SR04: HC-SR04 ultrasound distance sensor
